# Fritzing sketch silvia_power_control (saved by Fritzing 0.9.3b)
breadboards: 1

parts:
  Part1 = Arduino Uno (Rev3)
  Power_Switch = SPST Switch [package=r_sw_th]
  Q2 = Basic FET N-Channel [part_number=IRF520 package="TO220 [THT]"]
  R4 = Resistor [tolerance=±5% resistance=1k package=THT]
  OMRON1 = OMRON PCB Power Relay – G5LE [part_number=Relay package=THT]

nets:
  N1: Part1.D9_PWM, Q2.gate, R4.Pin_1
  N2: Part1.GND, Power_Switch.P, Q2.source, R4.Pin_0
  N3: Part1.D4, Power_Switch.O
  N4: Part1.VIN, OMRON1.COIL1
  N5: Q2.drain, OMRON1.COIL2

notes:
  Live In
  Relay
  Live Out
  G D S
  IRF520
  12V
